# Fritzing sketch button_passcode_schematic (saved by Fritzing 0.9.3b)
breadboards: 1

parts:
  Part1 = Arduino Uno (Rev3)
  S1 = Momentary Switch [package=ksa_sealed_tac_switch]
  S2 = Momentary Switch [package=ksa_sealed_tac_switch]
  S3 = Momentary Switch [package=ksa_sealed_tac_switch]
  LED1 = LED - 5mm [color="Red (633nm)" package="5 mm [THT]"]
  LED2 = LED - 5mm [color="Green (565nm)" package="5 mm [THT]"]
  R1 = Resistor [tolerance=±5% resistance=220 package=THT]
  R2 = Resistor [tolerance=±5% resistance=220 package=THT]

nets:
  N1: Part1.D8, S2.4
  N2: Part1.D9_PWM, S1.4
  N3: Part1.D10_PWM/SS, S3.4
  N4: Part1.GND, S1.2, S2.2, S3.2, LED1.cathode, LED2.cathode
  N5: Part1.D5_PWM, R2.Pin_1
  N6: Part1.D6_PWM, R1.Pin_1
  N7: LED1.anode, R1.Pin_0
  N8: LED2.anode, R2.Pin_0
