# Fritzing sketch digital_input_schematic (saved by Fritzing 0.9.3b)
breadboards: 1

parts:
  Part1 = Arduino Uno (Rev3)
  S1 = Momentary Switch [package=ksa_sealed_tac_switch]
  S2 = Momentary Switch [package=ksa_sealed_tac_switch]
  R1 = Resistor [tolerance=±5% resistance=220 package=THT]
  LED1 = LED - 5mm [color="Red (633nm)" package="5 mm [THT]"]

nets:
  N1: Part1.D8, S2.4
  N2: Part1.D9_PWM, S1.4
  N3: Part1.GND, S1.2, S2.2, LED1.cathode
  N4: Part1.D5_PWM, R1.Pin_1
  N5: R1.Pin_0, LED1.anode
