# Fritzing sketch lcd_schematic (saved by Fritzing 0.9.3b)
breadboards: 1

parts:
  U1 = LCD-16X2 [package=lcd-16x2_noholes]  # not connected
  Part1 = Arduino Uno (Rev3) - ICSP
  R1 = Trimmer Potentiometer [maximum_resistance=10kΩ package=THT]

nets:
  N1: Part1.GND, R1.leg2
  N2: Part1.5V, R1.leg1
