# Fritzing sketch servo_schematic (saved by Fritzing 0.9.3b)
breadboards: 1

parts:
  Part1 = Arduino Uno (Rev3)
  S1 = Momentary Switch [package=ksa_sealed_tac_switch]
  S2 = Momentary Switch [package=ksa_sealed_tac_switch]
  J1 = Basic Servo

nets:
  N1: Part1.D4, J1.pulse
  N2: Part1.D5_PWM, S1.3
  N3: Part1.D6_PWM, S2.3
  5V: Part1.5V, J1.vcc
  GND: Part1.GND, S1.1, S2.1, J1.gnd
