# Fritzing sketch stepmotor_schematic (saved by Fritzing 0.9.3b)
breadboards: 1

parts:
  Driver1 = 28BYJ-48 Driver Module [part_number=ULN2003 package=THT]
  Arduino = Arduino Uno (Rev3)
  SM1 = 28BYJ-48 Stepper Motor [part_number=28BYJ-48]  # not connected
  S1 = Pushbutton [package="[THT]"]
  S2 = Pushbutton [package="[THT]"]

nets:
  N1: Driver1.IN1, Arduino.D11_PWM/MOSI
  N2: Driver1.IN2, Arduino.D10_PWM/SS
  N3: Driver1.IN3, Arduino.D9_PWM
  N4: Driver1.IN4, Arduino.D8
  GND: Driver1.GND, Arduino.GND, S1.Pin_1, S1.Pin_2, S2.Pin_1, S2.Pin_2
  N5: Driver1.Vmotor, Arduino.5V
  N6: Arduino.D12/MISO, S1.Pin_3, S1.Pin_4
  N7: Arduino.D13/SCK, S2.Pin_3, S2.Pin_4

custom parts:
  28BYJ-48 Driver Module: Generic male header
  28BYJ-48 Stepper Motor: Unipolar Stepper Motor 28BYJ-48 Top coil - pink & orange Bottom coil - blue & yellow Common rail - red Connector pins: blue - pink - yellow - orange - red
