# Fritzing sketch rowLED (saved by Fritzing 0.9.3b)
breadboards: 1

parts:
  Part2 = Arduino Uno (Rev3)
  LED3 = LED - 5mm [color="Red (633nm)" package="5 mm [THT]"]
  LED4 = LED - 5mm [color="Red (633nm)" package="5 mm [THT]"]
  LED5 = LED - 5mm [color="Red (633nm)" package="5 mm [THT]"]
  LED6 = LED - 5mm [color="Red (633nm)" package="5 mm [THT]"]
  LED7 = LED - 5mm [color="Red (633nm)" package="5 mm [THT]"]
  R2 = Resistor [tolerance=±5% resistance=330 package="2512 [SMD]"]
  R3 = Resistor [tolerance=±5% resistance=330 package="2512 [SMD]"]
  R4 = Resistor [tolerance=±5% resistance=330 package="2512 [SMD]"]
  R5 = Resistor [tolerance=±5% resistance=330 package="2512 [SMD]"]
  R6 = Resistor [tolerance=±5% resistance=330 package="2512 [SMD]"]
  R7 = Rotary Potentiometer (Small) [maximum_resistance=100kΩ package=THT]  # not connected

nets:
  N1: Part2.D2, R5.Pin_1
  N2: Part2.D3_PWM, R4.Pin_1
  N3: Part2.D4, R3.Pin_1
  N4: Part2.D5_PWM, R2.Pin_1
  N5: Part2.D6_PWM, R6.Pin_1
  N6: Part2.5V, LED3.anode, LED4.anode, LED5.anode, LED6.anode, LED7.anode
  N7: LED3.cathode, R2.Pin_0
  N8: LED4.cathode, R3.Pin_0
  N9: LED5.cathode, R4.Pin_0
  N10: LED6.cathode, R5.Pin_0
  N11: LED7.cathode, R6.Pin_0
